# Fritzing sketch wiring_diagram (saved by Fritzing 0.9.2b)
circuit board: 8.46667cm x 5.64444cm
breadboards: 1

parts:
  R1 = Resistor [tolerance=±5% resistance=300 package=THT]
  LED1 = LED - 5mm [color="Yellow (585nm)" package="5 mm [THT]"]
  LED2 = LED - 5mm [color="Blue (470nm)" package="5 mm [THT]"]
  LED3 = LED - 5mm [color="Green (565nm)" package="5 mm [THT]"]
  LED4 = LED - 5mm [color="Red (635nm)" package="5 mm [THT]"]
  R2 = Resistor [tolerance=±5% resistance=300 package=THT]
  R3 = Resistor [tolerance=±5% resistance=300 package=THT]
  nodeMCU_esp8226 = NodeMCU V1.0
  R4 = Resistor [tolerance=±5% resistance=300 package=THT]

nets:
  N1: R1.Pin_0, nodeMCU_esp8226.D1
  N2: R1.Pin_1, LED1.anode
  N3: LED1.cathode, LED2.cathode, LED3.cathode, LED4.cathode, nodeMCU_esp8226.GND
  N4: LED2.anode, R2.Pin_1
  N5: LED3.anode, R3.Pin_1
  N6: LED4.anode, R4.Pin_1
  N7: R2.Pin_0, nodeMCU_esp8226.D2
  N8: R3.Pin_0, nodeMCU_esp8226.D3
  N9: nodeMCU_esp8226.D4, R4.Pin_0

custom parts:
  NodeMCU V1.0: ESP9266 based NodeMCU
